// Logisim project logica_booleana_da_soma_logisim.circ as structural Verilog: 1 circuit, main circuit main
module main (
  input  v1,
  input  v2,
  input  vai_um,
  output saida,
  output seta_vai_um
);

  wire nand_1_out, nand_2_out, nand_3_out, nand_4_out, nand_5_out, nand_6_out, nand_7_out, nand_8_out,
       nand_9_out, nand_10_out, nand_11_out, nand_12_out, nand_13_out, nand_14_out, nand_15_out, nand_16_out,
       nand_17_out, nand_18_out, nand_19_out, nand_20_out, nand_21_out, nand_22_out, nand_23_out,
       nand_25_out, nand_26_out, nand_27_out, nand_28_out;

  nand nand_1 (nand_1_out, v1, v1);
  nand nand_2 (nand_2_out, v2, v2);
  nand nand_3 (nand_3_out, v1, v1);
  nand nand_4 (nand_4_out, v2, v2);
  nand nand_5 (nand_5_out, v2, vai_um);
  nand nand_6 (nand_6_out, v1, vai_um);
  nand nand_7 (nand_7_out, nand_1_out, nand_2_out);
  nand nand_8 (nand_8_out, nand_3_out, v2);
  nand nand_9 (nand_9_out, v1, nand_4_out);
  nand nand_10 (nand_10_out, v1, v2);
  nand nand_11 (nand_11_out, nand_5_out, nand_6_out);
  nand nand_12 (nand_12_out, nand_7_out, nand_7_out);
  nand nand_13 (nand_13_out, nand_8_out, nand_8_out);
  nand nand_14 (nand_14_out, vai_um, vai_um);
  nand nand_15 (nand_15_out, nand_9_out, nand_9_out);
  nand nand_16 (nand_16_out, vai_um, vai_um);
  nand nand_17 (nand_17_out, nand_10_out, nand_10_out);
  nand nand_18 (nand_18_out, nand_11_out, nand_11_out);
  nand nand_19 (nand_19_out, v1, v2);
  nand nand_20 (nand_20_out, nand_12_out, vai_um);
  nand nand_21 (nand_21_out, nand_13_out, nand_14_out);
  nand nand_22 (nand_22_out, nand_15_out, nand_16_out);
  nand nand_23 (nand_23_out, nand_17_out, vai_um);
  nand nand_24 (seta_vai_um, nand_18_out, nand_19_out);
  nand nand_25 (nand_25_out, nand_20_out, nand_21_out);
  nand nand_26 (nand_26_out, nand_22_out, nand_23_out);
  nand nand_27 (nand_27_out, nand_25_out, nand_25_out);
  nand nand_28 (nand_28_out, nand_26_out, nand_26_out);
  nand nand_29 (saida, nand_27_out, nand_28_out);
endmodule
