// Logisim project calculo_erro_testado.circ as structural Verilog: 2 circuits, main circuit main
module main (
  input  r0,
  input  r1,
  output saida
);

  wire and_1_out, and_2_out, not_1_out, not_2_out;

  not not_1 (not_1_out, r0);
  not not_2 (not_2_out, r1);
  and and_1 (and_1_out, not_1_out, r1);
  and and_2 (and_2_out, r0, not_2_out);
  or or_1 (saida, and_1_out, and_2_out);
endmodule

module overflow (
  input  v2_1,
  input  c2_1,
  input  sr_2,
  output reseta
);

  and and_1 (reseta, v2_1, c2_1);
endmodule
