// Logisim project logica_booleana_erro_zero.circ as structural Verilog: 2 circuits, main circuit main
module main (
  input  i8,
  input  i7,
  input  i6,
  input  i5,
  input  i4,
  input  i3,
  input  i2,
  input  i1,
  input  i0,
  output erro,
  output zero
);

  wire and_1_out, and_2_out, and_3_out, and_4_out, and_5_out, and_6_out, and_7_out, and_8_out, not_1_out,
       not_2_out, not_3_out, not_4_out, not_5_out, not_6_out, not_7_out, not_8_out, not_9_out, not_10_out,
       not_11_out, not_12_out, not_13_out, not_14_out, not_15_out, not_16_out;

  not not_1 (not_1_out, i8);
  not not_2 (not_2_out, i7);
  not not_3 (not_3_out, i7);
  not not_4 (not_4_out, i7);
  not not_5 (not_5_out, i7);
  not not_6 (not_6_out, i7);
  not not_7 (not_7_out, i7);
  not not_8 (not_8_out, i7);
  not not_9 (not_9_out, i7);
  not not_10 (not_10_out, i6);
  not not_11 (not_11_out, i5);
  not not_12 (not_12_out, i4);
  not not_13 (not_13_out, i3);
  not not_14 (not_14_out, i2);
  not not_15 (not_15_out, i1);
  not not_16 (not_16_out, i0);
  and and_1 (and_1_out, not_1_out, i7);
  and and_2 (and_2_out, i8, not_2_out, i0);
  and and_3 (and_3_out, i8, not_3_out, i1);
  and and_4 (and_4_out, i8, not_4_out, i2);
  and and_5 (and_5_out, i8, not_5_out, i3);
  and and_6 (and_6_out, i8, not_6_out, i4);
  and and_7 (and_7_out, i8, not_7_out, i5);
  and and_8 (and_8_out, i8, not_8_out, i6);
  and and_9 (zero, not_9_out, not_10_out, not_11_out, not_12_out, not_13_out, not_14_out, not_15_out, not_16_out);
  or or_1 (erro, and_1_out, and_2_out, and_3_out, and_4_out, and_5_out, and_6_out, and_7_out, and_8_out);
endmodule

module operacao_erro_zero (
  input  subtracao,
  input  i8,
  input  i7,
  input  i6,
  input  i5,
  input  i4,
  input  i3,
  input  i2,
  input  i1,
  input  i0,
  output erro,
  output zero
);

  wire and_1_out, and_2_out, and_3_out, and_4_out, and_5_out, and_6_out, and_7_out, and_8_out, not_1_out,
       not_2_out, not_3_out, not_4_out, not_5_out, not_6_out, not_7_out, not_8_out, not_9_out, not_10_out,
       not_11_out, not_12_out, not_13_out, not_14_out, not_15_out, not_16_out, not_17_out;

  not not_1 (not_1_out, subtracao);
  not not_2 (not_2_out, i8);
  not not_3 (not_3_out, i7);
  not not_4 (not_4_out, i7);
  not not_5 (not_5_out, i7);
  not not_6 (not_6_out, i7);
  not not_7 (not_7_out, i7);
  not not_8 (not_8_out, i7);
  not not_9 (not_9_out, i7);
  not not_10 (not_10_out, i7);
  not not_11 (not_11_out, i6);
  not not_12 (not_12_out, i5);
  not not_13 (not_13_out, i4);
  not not_14 (not_14_out, i3);
  not not_15 (not_15_out, i2);
  not not_16 (not_16_out, i1);
  not not_17 (not_17_out, i0);
  and and_1 (and_1_out, not_1_out, not_2_out, i7);
  and and_2 (and_2_out, i8, not_3_out, i0);
  and and_3 (and_3_out, i8, not_4_out, i1);
  and and_4 (and_4_out, i8, not_5_out, i2);
  and and_5 (and_5_out, i8, not_6_out, i3);
  and and_6 (and_6_out, i8, not_7_out, i4);
  and and_7 (and_7_out, i8, not_8_out, i5);
  and and_8 (and_8_out, i8, not_9_out, i6);
  and and_9 (zero, not_10_out, not_11_out, not_12_out, not_13_out, not_14_out, not_15_out, not_16_out, not_17_out);
  or or_1 (erro, and_1_out, and_2_out, and_3_out, and_4_out, and_5_out, and_6_out, and_7_out, and_8_out);
endmodule
